# Fritzing sketch circuit-layout (saved by Fritzing 0.9.2b)
breadboards: 1

parts:
  Raspberry_Pi1 = Raspberry Pi 2
  IC1 = ADS1115 16-bit ADC Breakout
  U1 = RJ45 Jack [package=rj45-8]
  U2 = OP37 - Low Noise, Precision, High Speed Op Amp [part_number=ANA114]
  R1 = Resistor [tolerance=±1% resistance=33 package=THT]

nets:
  3V3: Raspberry_Pi1.3v3, IC1.VDD
  N1: Raspberry_Pi1.GPIO2, IC1.SDA
  N2: Raspberry_Pi1.GPIO3, IC1.SCL
  N3: Raspberry_Pi1.GPIO27, IC1.ALRT
  GND: Raspberry_Pi1.GND, IC1.GND, IC1.ADDR, U1.7, U2.-V, U2.NC
  N4: Raspberry_Pi1.5V, U1.8, U2.V+
  N5: U1.4, U2.-IN
  N6: U1.5, U2.+IN
  N7: U2.TRIM#8, R1.Pin_0

custom parts:
  ADS1115 16-bit ADC Breakout: ADS1015 12-bit I2C ADC+PGA Breakout
